# Fritzing sketch CeilingSpotlightSketch (saved by Fritzing 0.9.4)
circuit board: 8.46667cm x 5.64444cm

parts:
  Q1 = npn-Powertransistor [part_number="IRLZ 34N" package="TO220 [THT]"]
  Q2 = npn-Powertransistor [part_number="IRLZ 34N" package="TO220 [THT]"]
  IR1 = TSOP312.., 314.. [part_number=TSOP31238 package=THT]
  big_LED = LEDs [package=led10mm]
  little_LED = LEDs [package=led10mm]
  Power_plug1 = Power plug [part_number=12V]
  Attiny85 = Digispark
  status_LED_(red) = LEDs [package=led10mm]

nets:
  N1: Q1.base, Attiny85.P0
  N2: Q1.collector, big_LED.C
  GND: Q1.emitter, Q2.emitter, IR1.GND, Power_plug1.GND, Attiny85.GND, status_LED_(red).C
  N3: Q2.base, Attiny85.P4
  N4: Q2.collector, little_LED.C
  N5: IR1.Vs, Attiny85.VCC
  N6: IR1.Data, Attiny85.P2
  VCC: big_LED.A, little_LED.A, Power_plug1.VCC, Attiny85.VIN
  N7: Attiny85.P1, status_LED_(red).A

custom parts:
  Digispark: The Digispark is an Attiny85 based microcontroller development board similar to the Arduino line, only cheaper, smaller, and a bit less powerful. With a whole host of shields to extend its functionality and the ability to use the familiar Arduino IDE the Digispark is a great way to jump into electronics, or perfect for when an Arduino is too big or too much.
